# Fritzing sketch proto_screen_with_sensor (saved by Fritzing 0.9.3b)
circuit board: 8.46667cm x 5.64444cm
breadboards: 1

parts:
  Composant1 = Arduino Mega 2560 (Rev3)
  LCD1 = LCD screen
  R1 = Trimmer Potentiometer [maximum_resistance=10kΩ package=THT]
  S1 = Pushbutton [package="[THT]"]
  DHT1 = DHT11 Humitidy and Temperature Sensor
  ZS-042_RTC1 = ZS-042 RTC Module

nets:
  N1: Composant1.D20/SDA, Composant1.SDA, ZS-042_RTC1.SDA
  N2: Composant1.SCL, ZS-042_RTC1.SCL
  N3: Composant1.D12_PWM, LCD1.DB7
  N4: Composant1.D11_PWM, LCD1.DB6
  N5: Composant1.D10_PWM, LCD1.DB5
  N6: Composant1.D9_PWM, LCD1.DB4
  N7: Composant1.D8_PWM, LCD1.E
  VDD: Composant1.5V, LCD1.VDD, LCD1.LED+, R1.leg1, DHT1.VDD, ZS-042_RTC1.VCC
  GND: Composant1.GND, LCD1.VSS, LCD1.R/W, LCD1.LED-, R1.leg2, S1.Pin_1, S1.Pin_2, DHT1.GND, ZS-042_RTC1.GND
  N8: Composant1.D2_PWM, DHT1.DATA
  N9: Composant1.D6_PWM, S1.Pin_3, S1.Pin_4
  N10: Composant1.D7_PWM, LCD1.RS
  N11: LCD1.V0, R1.wiper

custom parts:
  DHT11 Humitidy and Temperature Sensor: DHT11 Humidity and Temperature Sensor
